# Fritzing sketch Projeto (saved by Fritzing 0.9.3b)

parts:
  RHT1 = Humidity and Temperature Sensor RHT03
  Componente1 = Arduino Uno (Rev3)
  KY-6 = Keyes Relay [package=THT]
  Espessif_Serial_Wifi_Modul_1 = ESP8266 ESP01 [part_number=ESP8266 package=THT]
  J1 = 120V duplex outlet_1  # not connected
  JACK1 = 2.1mm Barrel Jack with Terminal Block  # not connected

nets:
  VCC: RHT1.Vcc, Componente1.5V, KY-6.power, Espessif_Serial_Wifi_Modul_1.VCC
  N1: RHT1.Data-signal, Componente1.D7
  GND: RHT1.GND_2, Componente1.GND, KY-6.ground, Espessif_Serial_Wifi_Modul_1.GND
  N2: Componente1.D8, KY-6.signal
  N3: Componente1.D0/RX, Espessif_Serial_Wifi_Modul_1.TXD
  N4: Componente1.D1/TX, Espessif_Serial_Wifi_Modul_1.RXD

notes:
  Ligamos na 5v porem utilizando um adaptaor que faz a conversão de 5v para 3v

custom parts:
  Keyes Relay: The Keyes 5V relay module is suitable for SCM development, home appliance control. It uses a 5V~12V TIL control signal which can control DC / AC signal.
  ESP8266 ESP01: Generic WiFi Module based on the ESP8266 with onboard PCB antenna and UART communications
  120V duplex outlet_1: 120V duplex outlet.
